// Logisim project homework.circ as structural Verilog: 1 circuit, main circuit main
module main (
  input  X,
  input  Y,
  input  Q_t,
  output S,
  output Q_t_1
);

  wire and_1_out, and_2_out, and_3_out, xor_1_out;

  and and_1 (and_1_out, X, Y);
  and and_2 (and_2_out, X, Q_t);
  and and_3 (and_3_out, Y, Q_t);
  xor xor_1 (xor_1_out, X, Y);
  xor xor_2 (S, xor_1_out, Q_t);
  or or_1 (Q_t_1, and_1_out, and_2_out, and_3_out);
endmodule
